# Fritzing sketch sketch (saved by Fritzing 0.9.9b)

parts:
  MH-ET_LIVE_ESP32_DEVKIT1 = MH-ET LIVE ESP32 DEVKIT 38 pins
  LCD1 = 20x4 LCD display [part_number=2004A]
  HD1 = HD44780 [part_number="HD44780 IIC" chip_label=HD44780 package="DIP (Dual Inline) [THT]"]

nets:
  3V3: MH-ET_LIVE_ESP32_DEVKIT1.3V3, HD1.VCC
  GND: MH-ET_LIVE_ESP32_DEVKIT1.GND, HD1.GND
  N1: MH-ET_LIVE_ESP32_DEVKIT1.IO22, HD1.SCL
  N2: MH-ET_LIVE_ESP32_DEVKIT1.IO21, HD1.SDA
  VSS: LCD1.Vss, HD1.VSS
  VDD: LCD1.Vdd, HD1.VDD
  N3: LCD1.Vo, HD1.V0
  N4: LCD1.RS, HD1.RS
  N5: LCD1.R/W, HD1.RW
  N6: LCD1.E, HD1.E
  N7: LCD1.DB0, HD1.D0
  N8: LCD1.DB1, HD1.D1
  N9: LCD1.DB2, HD1.D2
  N10: LCD1.DB3, HD1.D3
  N11: LCD1.DB4, HD1.D4
  N12: LCD1.DB5, HD1.D5
  N13: LCD1.DB6, HD1.D6
  N14: LCD1.DB7, HD1.D7
  N15: LCD1.A_+, HD1.A
  N16: LCD1.K_-, HD1.K
  N17: HD1.LED_A, HD1.LED_B

custom parts:
  MH-ET LIVE ESP32 DEVKIT 38 pins: http://mh.nodebb.com/topic/2/mh-et-live-esp32-devkit
  20x4 LCD display: 20x4 character display. CHECK LED POLARITY BEFORE CONNECTING POWER Some versions of the dispaly have the polarity of the LED pins "A" and "K" reversed.
  HD44780: I2C-Module to use a 1602 or 2004 LCD on with the wire.h libory Serial LCD Modul
